# Fritzing sketch door_sensor_HW_diagram (saved by Fritzing 1.0.5)
breadboards: 1

parts:
  U1 = XIAO ESP32C3
  Mod1 = KY-021 Mini Magnetic Reed Switch Module [package="Breakout board"]

nets:
  N1: U1.D7, Mod1.S
  N2: U1.GND, Mod1.-
  5V: U1.5V, Mod1.Vin

custom parts:
  XIAO ESP32C3: Seeed Studio XIAO ESP32C3 adopts new RISC-V architecture, supporting both Wi-Fi and BLE wireless connectivities. For Internet of Things applications, you will find it is flexible and suitable for all kinds of IoT scenarios.
  KY-021 Mini Magnetic Reed Switch Module: KY-021 magnetic reed switch module. A reed switch is a magnetic sensor that is normally open and gets closed when exposed to a magnetic field.
